// Digital circuit register-file.dig as structural Verilog
module register_file (
  input  [4:0] ReadReg1,
  input  [4:0] ReadReg2,
  input  [4:0] WriteReg,
  input  [31:0] WriteData,
  input  RegWrite,
  input  Clock,
  output [31:0] ReadData1,
  output [31:0] ReadData2
);

  wire and_1_out, and_2_out, and_3_out, and_4_out, and_5_out, and_6_out, and_7_out, and_8_out, and_9_out,
       and_10_out, and_11_out, and_12_out, and_13_out, and_14_out, and_15_out, and_16_out, and_17_out,
       and_18_out, and_19_out, and_20_out, and_21_out, and_22_out, and_23_out, and_24_out, and_25_out,
       and_26_out, and_27_out, and_28_out, and_29_out, and_30_out, and_31_out, d0, d1, d2, d3, d4, d5, d6,
       d7, d8, d9, d10, d11, d12, d13, d14, d15, d16, d17, d18, d19, d20, d21, d22, d23, d24, d25, d26, d27,
       d28, d29, d30, d31;
  wire [31:0] O0, O1, O2, O3, O4, O5, O6, O7, O8, O9, O10, O11, O12, O13, O14, O15, O16, O17, O18, O19, O20,
       O21, O22, O23, O24, O25, O26, O27, O28, O29, O30, O31;

  Decoder #(.Selector_Bits(5)) decoder_1 (
    .sel(WriteReg), .out_0(d0), .out_1(d1), .out_2(d2), .out_3(d3), .out_4(d4), .out_5(d5), .out_6(d6),
    .out_7(d7), .out_8(d8), .out_9(d9), .out_10(d10), .out_11(d11), .out_12(d12), .out_13(d13), .out_14(d14),
    .out_15(d15), .out_16(d16), .out_17(d17), .out_18(d18), .out_19(d19), .out_20(d20), .out_21(d21),
    .out_22(d22), .out_23(d23), .out_24(d24), .out_25(d25), .out_26(d26), .out_27(d27), .out_28(d28),
    .out_29(d29), .out_30(d30), .out_31(d31));
  and and_1 (and_1_out, RegWrite, d21);
  and and_2 (and_2_out, RegWrite, d26);
  Register #(.Bits(32)) R0 (.D(WriteData), .C(Clock), .en(1'b0), .Q(O0));
  Register #(.Bits(32)) R21 (.D(WriteData), .C(Clock), .en(and_1_out), .Q(O21));
  Register #(.Bits(32)) R26 (.D(WriteData), .C(Clock), .en(and_2_out), .Q(O26));
  and and_3 (and_3_out, RegWrite, d1);
  and and_4 (and_4_out, RegWrite, d2);
  and and_5 (and_5_out, RegWrite, d3);
  and and_6 (and_6_out, RegWrite, d4);
  and and_7 (and_7_out, RegWrite, d5);
  and and_8 (and_8_out, RegWrite, d6);
  and and_9 (and_9_out, RegWrite, d7);
  and and_10 (and_10_out, RegWrite, d8);
  and and_11 (and_11_out, RegWrite, d9);
  and and_12 (and_12_out, RegWrite, d10);
  and and_13 (and_13_out, RegWrite, d11);
  and and_14 (and_14_out, RegWrite, d22);
  and and_15 (and_15_out, RegWrite, d27);
  Register #(.Bits(32)) R1 (.D(WriteData), .C(Clock), .en(and_3_out), .Q(O1));
  Register #(.Bits(32)) R2 (.D(WriteData), .C(Clock), .en(and_4_out), .Q(O2));
  Register #(.Bits(32)) R3 (.D(WriteData), .C(Clock), .en(and_5_out), .Q(O3));
  Register #(.Bits(32)) R4 (.D(WriteData), .C(Clock), .en(and_6_out), .Q(O4));
  Register #(.Bits(32)) R5 (.D(WriteData), .C(Clock), .en(and_7_out), .Q(O5));
  Register #(.Bits(32)) R6 (.D(WriteData), .C(Clock), .en(and_8_out), .Q(O6));
  Register #(.Bits(32)) R7 (.D(WriteData), .C(Clock), .en(and_9_out), .Q(O7));
  Register #(.Bits(32)) R8 (.D(WriteData), .C(Clock), .en(and_10_out), .Q(O8));
  Register #(.Bits(32)) R9 (.D(WriteData), .C(Clock), .en(and_11_out), .Q(O9));
  Register #(.Bits(32)) R10 (.D(WriteData), .C(Clock), .en(and_12_out), .Q(O10));
  Register #(.Bits(32)) R11 (.D(WriteData), .C(Clock), .en(and_13_out), .Q(O11));
  Register #(.Bits(32)) R22 (.D(WriteData), .C(Clock), .en(and_14_out), .Q(O22));
  Register #(.Bits(32)) R27 (.D(WriteData), .C(Clock), .en(and_15_out), .Q(O27));
  and and_16 (and_16_out, RegWrite, d23);
  and and_17 (and_17_out, RegWrite, d28);
  and and_18 (and_18_out, RegWrite, d12);
  and and_19 (and_19_out, RegWrite, d13);
  and and_20 (and_20_out, RegWrite, d14);
  and and_21 (and_21_out, RegWrite, d15);
  and and_22 (and_22_out, RegWrite, d16);
  and and_23 (and_23_out, RegWrite, d17);
  and and_24 (and_24_out, RegWrite, d18);
  and and_25 (and_25_out, RegWrite, d19);
  and and_26 (and_26_out, RegWrite, d20);
  Register #(.Bits(32)) R12 (.D(WriteData), .C(Clock), .en(and_18_out), .Q(O12));
  Register #(.Bits(32)) R13 (.D(WriteData), .C(Clock), .en(and_19_out), .Q(O13));
  Register #(.Bits(32)) R14 (.D(WriteData), .C(Clock), .en(and_20_out), .Q(O14));
  Register #(.Bits(32)) R15 (.D(WriteData), .C(Clock), .en(and_21_out), .Q(O15));
  Register #(.Bits(32)) R16 (.D(WriteData), .C(Clock), .en(and_22_out), .Q(O16));
  Register #(.Bits(32)) R17 (.D(WriteData), .C(Clock), .en(and_23_out), .Q(O17));
  Register #(.Bits(32)) R18 (.D(WriteData), .C(Clock), .en(and_24_out), .Q(O18));
  Register #(.Bits(32)) R19 (.D(WriteData), .C(Clock), .en(and_25_out), .Q(O19));
  Register #(.Bits(32)) R20 (.D(WriteData), .C(Clock), .en(and_26_out), .Q(O20));
  Register #(.Bits(32)) R23 (.D(WriteData), .C(Clock), .en(and_16_out), .Q(O23));
  Register #(.Bits(32)) R28 (.D(WriteData), .C(Clock), .en(and_17_out), .Q(O28));
  and and_27 (and_27_out, RegWrite, d24);
  and and_28 (and_28_out, RegWrite, d29);
  Multiplexer #(.Bits(32), .Selector_Bits(5)) multiplexer_1 (
    .sel(ReadReg1), .in_0(O0), .in_1(O1), .in_2(O2), .in_3(O3), .in_4(O4), .in_5(O5), .in_6(O6), .in_7(O7),
    .in_8(O8), .in_9(O9), .in_10(O10), .in_11(O11), .in_12(O12), .in_13(O13), .in_14(O14), .in_15(O15),
    .in_16(O16), .in_17(O17), .in_18(O18), .in_19(O19), .in_20(O20), .in_21(O21), .in_22(O22), .in_23(O23),
    .in_24(O24), .in_25(O25), .in_26(O26), .in_27(O27), .in_28(O28), .in_29(O29), .in_30(O30), .in_31(O31),
    .out(ReadData1));
  Register #(.Bits(32)) R24 (.D(WriteData), .C(Clock), .en(and_27_out), .Q(O24));
  Register #(.Bits(32)) R29 (.D(WriteData), .C(Clock), .en(and_28_out), .Q(O29));
  Multiplexer #(.Bits(32), .Selector_Bits(5)) multiplexer_2 (
    .sel(ReadReg2), .in_0(O0), .in_1(O1), .in_2(O2), .in_3(O3), .in_4(O4), .in_5(O5), .in_6(O6), .in_7(O7),
    .in_8(O8), .in_9(O9), .in_10(O10), .in_11(O11), .in_12(O12), .in_13(O13), .in_14(O14), .in_15(O15),
    .in_16(O16), .in_17(O17), .in_18(O18), .in_19(O19), .in_20(O20), .in_21(O21), .in_22(O22), .in_23(O23),
    .in_24(O24), .in_25(O25), .in_26(O26), .in_27(O27), .in_28(O28), .in_29(O29), .in_30(O30), .in_31(O31),
    .out(ReadData2));
  and and_29 (and_29_out, RegWrite, d25);
  and and_30 (and_30_out, RegWrite, d30);
  Register #(.Bits(32)) R25 (.D(WriteData), .C(Clock), .en(and_29_out), .Q(O25));
  Register #(.Bits(32)) R30 (.D(WriteData), .C(Clock), .en(and_30_out), .Q(O30));
  and and_31 (and_31_out, RegWrite, d31);
  Register #(.Bits(32)) R31 (.D(WriteData), .C(Clock), .en(and_31_out), .Q(O31));

  // Other names for the same wires on the sheet: RegW = RegWrite
endmodule

/* Test case Register File Test:
WriteReg WriteData RegWrite Clock ReadReg1 ReadReg2 ReadData1 ReadData2

# $1 = 25
1 25 1 C 1 0 25 0

# $2 = 30
2 30 1 C 0 2 0 30

# $(N+1) = (N+1)
loop(N, 30)
	(N+1) (N+1) 1 C (N+1) (N) (N+1) (N)
end loop

# $(N+1) = N-60
loop(N, 30)
	(N+1) (N-60) 1 C (N+1) (N+1) (N-60) (N-60)
end loop

# Try writing to $0. This should not write anything
0 25 1 C 0 0 0 0

# try writing when RegWrite = 0
# (the registers should still have their old values)
loop(N, 30)
	(N+1) (N+80) 0 C (N+1) (N+1) (N-60) (N-60)
end loop
*/
