// Digital circuit control-unit.dig as structural Verilog
module control_unit (
  input  [6:0] opcode,
  input  [2:0] funct3,
  input  [6:0] funct7,
  output RegWrite,
  output ALUSrc,
  output ImmSrc1,
  output ALUOp0,
  output is_add,
  output is_sub,
  output is_and,
  output is_or,
  output is_slt,
  output is_addi,
  output is_slti,
  output is_andi,
  output ImmSrc0,
  output ALUOp1,
  output ALUOp2,
  output ALUOp3
);

  wire comparator_1_eq, comparator_2_eq, comparator_3_eq, comparator_4_eq, comparator_5_eq, comparator_6_eq,
       comparator_7_eq, comparator_8_eq;
  wire [2:0] priorityencoder_1_num;

  Comparator #(.Bits(7)) comparator_1 (.a(funct7), .b({7{1'b0}}), .eq(comparator_1_eq));  // open: gt, lt
  Comparator #(.Bits(7)) comparator_2 (.a(funct7), .b(7'b0100000), .eq(comparator_2_eq));  // open: gt, lt
  Comparator #(.Bits(3)) comparator_3 (.a(funct3), .b(3'b111), .eq(comparator_3_eq));  // open: gt, lt
  Comparator #(.Bits(3)) comparator_4 (.a(funct3), .b(3'b110), .eq(comparator_4_eq));  // open: gt, lt
  Comparator #(.Bits(3)) comparator_5 (.a(funct3), .b(3'b010), .eq(comparator_5_eq));  // open: gt, lt
  Comparator #(.Bits(7)) comparator_6 (.a(7'b0110011), .b(opcode), .eq(comparator_6_eq));  // open: gt, lt
  Comparator #(.Bits(3)) comparator_7 (.a(funct3), .b(3'b000), .eq(comparator_7_eq));  // open: gt, lt
  and and_1 (is_add, comparator_6_eq, comparator_7_eq, comparator_1_eq);
  and and_2 (is_sub, comparator_6_eq, comparator_7_eq, comparator_2_eq);
  and and_3 (is_and, comparator_6_eq, comparator_3_eq, comparator_1_eq);
  and and_4 (is_or, comparator_6_eq, comparator_4_eq, comparator_1_eq);
  and and_5 (is_slt, comparator_6_eq, comparator_5_eq, comparator_1_eq);
  Comparator #(.Bits(7)) comparator_8 (.a(7'b0010011), .b(opcode), .eq(comparator_8_eq));  // open: gt, lt
  and and_6 (is_addi, comparator_8_eq, comparator_7_eq);
  and and_7 (is_slti, comparator_8_eq, comparator_5_eq);
  and and_8 (is_andi, comparator_8_eq, comparator_3_eq);
  PriorityEncoder #(.Selector_Bits(3)) priorityencoder_1 (
    .in0(is_add), .in1(is_sub), .in2(is_and), .in3(is_or), .in4(is_slt), .in5(is_addi), .in6(is_slti),
    .in7(is_andi), .num(priorityencoder_1_num));  // open: any
  ROM #(.AddrBits(3), .Bits(8)) rom_1 (
    .A(priorityencoder_1_num), .sel(1'b1),
    .D({RegWrite, ALUSrc, ImmSrc1, ImmSrc0, ALUOp3, ALUOp2, ALUOp1, ALUOp0}));

  // Notes on the sheet:
  //   contents of rom_1 (hex, n*v repeats v):
  //   82,86,80,81,87,c2,c7,c0
endmodule

/* Test case Test:
opcode    funct3  funct7     RegWrite ALUSrc ImmSrc1 ImmSrc0 ALUOp3 ALUOp2 ALUOp1 ALUOp0
# add
0b0110011 0b000   0b0000000  0b1      0b0    0b0     0b0     0b0    0b0    0b1    0b0
# sub
0b0110011 0b000   0b0100000  0b1      0b0    0b0     0b0     0b0    0b1    0b1    0b0
# and
0b0110011 0b111   0b0000000  0b1      0b0    0b0     0b0     0b0    0b0    0b0    0b0
# or
0b0110011 0b110   0b0000000  0b1      0b0    0b0     0b0     0b0    0b0    0b0    0b1
# slt
0b0110011 0b010   0b0000000  0b1      0b0    0b0     0b0     0b0    0b1    0b1    0b1
# addi
0b0010011 0b000   0b0000000  0b1      0b1    0b0     0b0     0b0    0b0    0b1    0b0
# slti
0b0010011 0b010   0b0000000  0b1      0b1    0b0     0b0     0b0    0b1    0b1    0b1
# andi
0b0010011 0b111   0b0000000  0b1      0b1    0b0     0b0     0b0    0b0    0b0    0b0
*/
