// Digital circuit cpu.dig as structural Verilog
module cpu (
  input  clk,
  output [31:0] ReadData1,
  output [31:0] ReadData2,
  output [6:0] opcode,
  output [4:0] rd,
  output [2:0] funct3,
  output [4:0] rs1,
  output [4:0] rs2,
  output [6:0] funct7
);

  wire control_unit_1_p4, control_unit_1_p5;
  wire [3:0] control_unit_1_p6;
  wire [31:0] add_1_s, alu_1_result, bitextender_1_out, multiplexer_1_out, PC_q, register_file_1_readdata2;

  Register #(.Bits(32), .isProgramCounter("true")) PC (.D(add_1_s), .C(clk), .en(1'b1), .Q(PC_q));
  Add #(.Bits(32)) add_1 (.a(32'h4), .b(PC_q), .c_i(1'b0), .s(add_1_s));  // open: c_o
  ROM #(.AddrBits(10), .isProgramMemory("true"), .Bits(32)) Instruction_Memory (
    .A(PC_q[11:2]), .sel(1'b1), .D({funct7, rs2, rs1, funct3, rd, opcode}));
  BitExtender #(.inputBits(12), .outputBits(32)) bitextender_1 (.in({funct7, rs2}), .out(bitextender_1_out));
  // control_unit control_unit_1: pin names not known; wires that end beside it: opcode, funct3, funct7, control_unit_1_p4, control_unit_1_p5, control_unit_1_p6[0], control_unit_1_p6[1], control_unit_1_p6[2], control_unit_1_p6[3]
  register_file register_file_1 (
    .ReadReg1(rs1), .ReadReg2(rs2), .WriteReg(rd), .WriteData(alu_1_result), .RegWrite(control_unit_1_p4),
    .Clock(clk), .ReadData1(ReadData1), .ReadData2(register_file_1_readdata2));
  Multiplexer #(.Bits(32)) multiplexer_1 (
    .sel(control_unit_1_p5), .in_0(register_file_1_readdata2), .in_1(bitextender_1_out),
    .out(multiplexer_1_out));
  alu alu_1 (
    .A(ReadData1), .B(multiplexer_1_out), .ALUOperation(control_unit_1_p6), .Result(alu_1_result));  // open: FlagZ

  assign ReadData2 = {32{1'b0}};

  // Other names for the same wires on the sheet: clock = clk

  // Notes on the sheet:
  //   contents of Instruction_Memory (hex, n*v repeats v):
  //   fec00213,7f020293,70128313,53130393,12337713,71c77793,5417f893
  //   ,13722913,292993,9aa13,ffda2a93,5aab13,b0013,fec22b93,b8013,fa65ac13
  //   ,c0013,22c93,c8013,2585ad13,d0013,fff22d93,d8013
endmodule

/* Test case cpu:
clk ReadData1 ReadData2
0 0 0        # addi x4, x0, -20
C (-20) 0    # addi x5, x4, 0x7F0      ; x4 = -20
C 2012 0     # addi x6, x5, 0x701      ; x5 = 2012
C 3805 0     # addi x7, x6, 0x531      ; x6 = 3805
C 3805 0     # andi x14, x6, 0x123     ; rs1 = x6
C 1 0        # andi x15, x14, 0x71C    ; rs1 = x14 = 1
C 0 0        # andi x17, x15, 0x541    ; rs1 = x15 = 0
C (-20) 0    # slti x18, x4, 311       ; rs1 = x4
C 1 0        # slti x19, x18, 2        ; rs1 = x18 = 1
C 1 0        # slti x20, x19, 0        ; rs1 = x19 = 1
C 0 0        # slti x21, x20, -3       ; rs1 = x20 = 0
C 0 0        # slti x22, x21, 5        ; rs1 = x21 = 0
C 1 0        # addi x0,  x22, 0        ; rs1 = x22 = 1 (write to x0 ignored)
C (-20) 0    # slti x23, x4,  -20      ; rs1 = x4
C 0 0        # addi x0,  x23, 0        ; rs1 = x23 = 0
C 0 0        # slti x24, x11, -90      ; x11 was never set, so 0
C 0 0        # addi x0,  x24, 0        ; rs1 = x24 = 0
C (-20) 0    # slti x25, x4,  0        ; rs1 = x4
C 1 0        # addi x0,  x25, 0        ; rs1 = x25 = 1
C 0 0        # slti x26, x11, 600      ; x11 still 0
C 1 0        # addi x0,  x26, 0        ; rs1 = x26 = 1
C (-20) 0    # slti x27, x4,  -1       ; rs1 = x4
C 1 0        # addi x0,  x27, 0        ; rs1 = x27 = 1
*/
